// Logisim project hw2-q2-circuit.circ as structural Verilog: 1 circuit, main circuit main
module main (
  input  A,
  input  A_2,
  input  B,
  input  B_2,
  input  C,
  input  C_2,
  input  D,
  input  D_2,
  input  A_3,
  input  A_4,
  input  B_3,
  input  B_4,
  input  C_3,
  input  C_4,
  input  D_3,
  input  D_4,
  output out_17,
  output out_18,
  output out_19,
  output out_20
);

  wire and_1_out, and_2_out, and_3_out, and_4_out, and_5_out, and_6_out, nand_1_out, nand_2_out, nand_3_out,
       nand_4_out, nand_5_out, nand_6_out, nand_7_out, nand_8_out, nand_9_out, nand_10_out, nand_11_out,
       nand_12_out, not_1_out, not_2_out, not_3_out, not_4_out, not_5_out, not_6_out;

  not not_1 (not_1_out, A_3);
  not not_2 (not_2_out, C_3);
  and and_1 (and_1_out, B, C);
  not not_3 (not_3_out, B);
  not not_4 (not_4_out, D);
  not not_5 (not_5_out, B_3);
  and and_2 (and_2_out, B_3, not_2_out, not_6_out);
  not not_6 (not_6_out, D_3);
  and and_3 (and_3_out, A, D);
  and and_4 (and_4_out, not_3_out, not_4_out);
  and and_5 (and_5_out, not_1_out, D_3, not_5_out);
  and and_6 (and_6_out, not_1_out, B_3, not_2_out);
  or or_1 (out_17, and_3_out, and_1_out, and_4_out);
  or or_2 (out_19, and_5_out, and_6_out, and_2_out);
  nand nand_1 (nand_1_out, A_4, A_4);
  nand nand_2 (nand_2_out, C_4, C_4);
  nand nand_3 (nand_3_out, B_2, C_2);
  nand nand_4 (nand_4_out, B_2, B_2);
  nand nand_5 (nand_5_out, D_2, D_2);
  nand nand_6 (nand_6_out, B_4, B_4);
  nand nand_7 (nand_7_out, D_4, D_4);
  nand nand_8 (nand_8_out, A_2, D_2);
  nand nand_9 (nand_9_out, nand_4_out, nand_5_out);
  nand nand_10 (nand_10_out, nand_1_out, nand_6_out);
  nand nand_11 (nand_11_out, nand_1_out, nand_2_out);
  nand nand_12 (nand_12_out, B_4, nand_7_out);
  nand nand_13 (out_18, nand_8_out, nand_3_out, nand_9_out);
  nand nand_14 (out_20, nand_10_out, nand_11_out, nand_12_out);

  // Notes on the sheet:
  //   F
  //   F'
  //   F with only nand gates
  //   F' with only nand gates
endmodule
