// Logisim project cse222-hw3.circ as structural Verilog: 1 circuit, main circuit main
module main (
  input  a,
  output x,
  output y,
  output z
);

  wire and_1_out, and_2_out, and_4_out, and_5_out, and_6_out, and_7_out, and_8_out, and_9_out, and_10_out,
       and_11_out, and_12_out, clock_1_out, nand_1_out, not_1_out, not_2_out, not_3_out, not_4_out,
       not_5_out, not_6_out, not_7_out, not_8_out, not_9_out, not_10_out, not_11_out, not_12_out, not_13_out,
       or_1_out, or_3_out, or_4_out, or_5_out, or_7_out, or_8_out, or_9_out, S0_q, S1_q, S2_q;

  Clock clock_1 (.out(clock_1_out));
  Register #(.width(1)) S2 (.D(or_8_out), .en(1'b1), .Q(S2_q), .clk(clock_1_out));  // open: clr
  Register #(.width(1)) S1 (.D(or_7_out), .en(1'b1), .Q(S1_q), .clk(clock_1_out));  // open: clr
  Register #(.width(1)) S0 (.D(or_9_out), .en(1'b1), .Q(S0_q), .clk(clock_1_out));  // open: clr
  and and_1 (and_1_out, S1_q, not_1_out);
  not not_1 (not_1_out, S0_q);
  and and_2 (and_2_out, S2_q, S0_q);
  not not_2 (not_2_out, S2_q);
  or or_1 (or_1_out, S2_q, S0_q);
  not not_3 (not_3_out, S1_q);
  not not_4 (not_4_out, S2_q);
  not not_5 (not_5_out, S0_q);
  not not_6 (not_6_out, a);
  or or_2 (x, and_1_out, and_2_out);
  and and_3 (y, not_2_out, or_3_out);
  or or_3 (or_3_out, S1_q, S0_q);
  and and_4 (and_4_out, or_1_out, not_3_out);
  not not_7 (not_7_out, S2_q);
  and and_5 (and_5_out, not_7_out, S1_q, not_8_out);
  not not_8 (not_8_out, S0_q);
  not not_9 (not_9_out, S1_q);
  or or_4 (or_4_out, not_9_out, not_10_out);
  not not_10 (not_10_out, a);
  and and_6 (and_6_out, not_4_out, not_5_out);
  or or_5 (or_5_out, and_6_out, not_6_out);
  not not_11 (not_11_out, S1_q);
  or or_6 (z, and_4_out, and_5_out);
  and and_7 (and_7_out, or_4_out, S2_q);
  and and_8 (and_8_out, S0_q, S1_q, a);
  and and_9 (and_9_out, or_5_out, S1_q);
  or or_7 (or_7_out, and_9_out, and_10_out);
  and and_10 (and_10_out, not_11_out, S0_q, a);
  or or_8 (or_8_out, and_7_out, and_8_out);
  not not_12 (not_12_out, S0_q);
  nand nand_1 (nand_1_out, S2_q, S1_q);
  and and_11 (and_11_out, nand_1_out, not_12_out, a);
  and and_12 (and_12_out, S0_q, not_13_out);
  not not_13 (not_13_out, a);
  or or_9 (or_9_out, and_11_out, and_12_out);

  // Notes on the sheet:
  //                   000,011,111,010,001,101,100, repeat
endmodule
