// Logisim project 1901042631.circ as structural Verilog: 1 circuit, main circuit main
module main (
  input  A,
  input  B,
  input  C,
  input  D,
  output out_5,
  output out_6
);

  wire not_1_out, not_2_out, not_3_out;

  not not_1 (not_1_out, C);
  not not_2 (not_2_out, B);
  and and_1 (out_5, not_2_out, not_3_out);
  not not_3 (not_3_out, D);
  and and_2 (out_6, not_2_out, not_1_out);
endmodule
