// Logisim project lab3.circ as structural Verilog: 1 circuit, main circuit main
module main (
  input  A,
  input  in_2,
  input  in_3,
  input  in_4,
  input  in_5,
  output out_6
);

  wire and_1_out, and_2_out, and_3_out, not_1_out, not_2_out, xnor_1_out, xnor_2_out;

  not not_1 (not_1_out, A);
  not not_2 (not_2_out, in_2);
  and and_1 (and_1_out, not_1_out, not_2_out, in_3, in_5);
  NotExactlyOne xnor_1 (.out(xnor_1_out), .in0(A), .in1(in_3), .in2(in_4), .in3(in_5));
  NotExactlyOne xnor_2 (.out(xnor_2_out), .in0(in_3), .in1(in_4), .in2(in_5));
  and and_2 (and_2_out, A, xnor_1_out, not_2_out);
  and and_3 (and_3_out, xnor_2_out, in_2);
  or or_1 (out_6, and_1_out, and_2_out, and_3_out);
endmodule
