// Logisim project lab4.circ as structural Verilog: 1 circuit, main circuit main
module main (
  input  A,
  input  B,
  input  in_3
);

  wire and_1_out, and_2_out, and_3_out, and_4_out, and_5_out, and_6_out, clock_1_out, not_1_out, not_2_out,
       not_3_out, not_4_out, not_5_out, or_1_out, or_2_out, register_1_q;

  not not_1 (not_1_out, register_1_q);
  not not_2 (not_2_out, B);
  and and_1 (and_1_out, not_2_out, A, not_1_out);
  and and_2 (and_2_out, B, register_1_q, or_2_out);
  or or_1 (or_1_out, and_2_out, and_1_out, and_4_out);
  not not_3 (not_3_out, A);
  not not_4 (not_4_out, or_2_out);
  and and_3 (and_3_out, not_3_out, register_1_q, not_4_out);
  and and_4 (and_4_out, not_3_out, or_2_out, register_1_q);
  Clock clock_1 (.out(clock_1_out));
  not not_5 (not_5_out, register_1_q);
  and and_5 (and_5_out, B, register_1_q);
  and and_6 (and_6_out, A, not_5_out, or_2_out);
  or or_2 (or_2_out, and_3_out, and_6_out, and_5_out);
  Register #(.width(1)) register_1 (.D(or_2_out), .en(in_3), .Q(register_1_q), .clk(clock_1_out));  // open: clr
  LED led_1 (.in(register_1_q));
  Register #(.width(1)) register_2 (.D(or_1_out), .en(in_3), .Q(or_2_out), .clk(clock_1_out));  // open: clr

  // Notes on the sheet:
  //   D0
  //   D1
endmodule
