// Logisim project HW4.circ as structural Verilog: 1 circuit, main circuit main
module main (
  input  I5,
  input  in_2,
  input  in_3,
  input  I0,
  input  in_5,
  input  I0_2,
  input  clear,
  input  load,
  input  swap,
  output out_10,
  output out_11,
  output out_12,
  output out_13,
  output out_14,
  output out_15
);

  wire and_1_out, clock_1_out, multiplexer_1_out, multiplexer_2_out, multiplexer_3_out, multiplexer_4_out,
       multiplexer_5_out, multiplexer_6_out, not_1_out;
  wire [1:0] S0_out;

  or S1 (S0_out[1], clear, load);
  not not_1 (not_1_out, load);
  and and_1 (and_1_out, not_1_out, swap);
  or S0 (S0_out[0], and_1_out, clear);
  Multiplexer #(.select(2)) multiplexer_1 (
    .in0(out_10), .in1(in_2), .in2(I5), .in3(1'b0), .out(multiplexer_1_out), .sel(S0_out));  // open: en
  Clock clock_1 (.out(clock_1_out));
  D_Flip_Flop d_ff_1 (.clk(clock_1_out), .D(multiplexer_1_out), .Q(out_10));  // open: Qn, preset, en, reset
  Multiplexer #(.select(2)) multiplexer_2 (
    .in0(out_11), .in1(I5), .in2(in_2), .in3(1'b0), .out(multiplexer_2_out), .sel(S0_out));  // open: en
  D_Flip_Flop d_ff_2 (.clk(clock_1_out), .D(multiplexer_2_out), .Q(out_11));  // open: Qn, preset, en, reset
  Multiplexer #(.select(2)) multiplexer_3 (
    .in0(out_12), .in1(I0), .in2(in_3), .in3(1'b0), .out(multiplexer_3_out), .sel(S0_out));  // open: en
  D_Flip_Flop d_ff_3 (.clk(clock_1_out), .D(multiplexer_3_out), .Q(out_12));  // open: Qn, preset, en, reset
  Multiplexer #(.select(2)) multiplexer_4 (
    .in0(out_13), .in1(in_3), .in2(I0), .in3(1'b0), .out(multiplexer_4_out), .sel(S0_out));  // open: en
  D_Flip_Flop d_ff_4 (.clk(clock_1_out), .D(multiplexer_4_out), .Q(out_13));  // open: Qn, preset, en, reset
  Multiplexer #(.select(2)) multiplexer_5 (
    .in0(out_14), .in1(I0_2), .in2(in_5), .in3(1'b0), .out(multiplexer_5_out), .sel(S0_out));  // open: en
  D_Flip_Flop d_ff_5 (.clk(clock_1_out), .D(multiplexer_5_out), .Q(out_14));  // open: Qn, preset, en, reset
  Multiplexer #(.select(2)) multiplexer_6 (
    .in0(out_15), .in1(in_5), .in2(I0_2), .in3(1'b0), .out(multiplexer_6_out), .sel(S0_out));  // open: en
  D_Flip_Flop d_ff_6 (.clk(clock_1_out), .D(multiplexer_6_out), .Q(out_15));  // open: Qn, preset, en, reset
endmodule
