// Logisim project LAB5-CIRCUIT.circ as structural Verilog: 1 circuit, main circuit main
module main (
  input  req,
  input  p3s,
  input  p7s,
  input  p37s,
  output resetT
);

  wire and_2_out, and_3_out, and_4_out, and_5_out, and_6_out, and_7_out, and_8_out, and_9_out, clock_1_out,
       not_1_out, not_2_out, not_3_out, not_4_out, not_5_out, not_6_out, or_1_out, or_2_out, S0_q, S1_q;

  Clock clock_1 (.out(clock_1_out));
  Register #(.width(1)) S1 (.D(or_1_out), .en(1'b1), .Q(S1_q), .clk(clock_1_out));  // open: clr
  not not_1 (not_1_out, S1_q);
  Register #(.width(1)) S0 (.D(or_2_out), .en(1'b1), .Q(S0_q), .clk(clock_1_out));  // open: clr
  not not_2 (not_2_out, req);
  and and_1 (resetT, not_2_out, not_1_out, not_3_out);
  not not_3 (not_3_out, S0_q);
  and and_2 (and_2_out, S0_q, not_1_out, p3s);
  and and_3 (and_3_out, S0_q, S1_q, not_4_out);
  not not_4 (not_4_out, p37s);
  and and_4 (and_4_out, S1_q, not_5_out);
  not not_5 (not_5_out, S0_q);
  and and_5 (and_5_out, not_5_out, not_6_out);
  not not_6 (not_6_out, S1_q);
  and and_6 (and_6_out, S0_q, S1_q, p37s);
  and and_7 (and_7_out, S1_q, not_3_out);
  and and_8 (and_8_out, S1_q, S0_q);
  or or_1 (or_1_out, and_2_out, and_3_out, and_4_out);
  and and_9 (and_9_out, and_4_out, p7s);
  LED RED (.in(not_1_out));
  LED ORANGE (.in(and_7_out));
  LED GREEN (.in(and_8_out));
  or or_2 (or_2_out, and_5_out, and_9_out, and_6_out);
endmodule
