// Logisim project lab6.circ as structural Verilog: 1 circuit, main circuit main
module main (
  input  [7:0] x,
  input  [7:0] y,
  input  goi,
  input  z_ld,
  input  z_clr,
  output diff_lgr,
  output diff_lgr_10
);

  wire not_1_out;
  wire [7:0] adder_1_out, adder_2_out, diff2_reg_q, diff_reg_q, multiplexer_1_out, multiplexer_2_out,
       subtractor_1_out, subtractor_2_out, z_reg_q;

  not not_1 (not_1_out, diff_lgr_10);
  Multiplexer #(.width(8)) multiplexer_1 (
    .in0(adder_1_out), .in1(adder_2_out), .out(multiplexer_1_out), .sel(diff_lgr_10), .en(not_1_out));
  Subtractor subtractor_1 (.a(x), .b(y), .out(subtractor_1_out));  // open: bin, bout
  Register z_reg (.D(multiplexer_1_out), .en(z_ld), .Q(z_reg_q), .clr(z_clr));  // open: clk
  Multiplexer #(.width(8)) multiplexer_2 (
    .in0(subtractor_1_out), .in1(subtractor_2_out), .out(multiplexer_2_out), .sel(diff_lgr), .en(goi));
  Register diff_reg (.D(multiplexer_2_out), .Q(diff_reg_q));  // open: en, clk, clr
  Adder adder_1 (.a(z_reg_q), .b(diff2_reg_q), .out(adder_1_out));  // open: cin, cout
  Register diff2_reg (.D(diff_reg_q), .Q(diff2_reg_q));  // open: en, clk, clr
  Comparator comparator_1 (.a(diff_reg_q), .b({8{1'b0}}), .gt(diff_lgr));  // open: eq, lt
  Comparator comparator_2 (.a(diff_reg_q), .b(8'ha), .gt(diff_lgr_10));  // open: eq, lt
  Adder adder_2 (.a(z_reg_q), .b(8'h5), .out(adder_2_out));  // open: cin, cout
  Subtractor subtractor_2 (.a(diff_reg_q), .b(8'h1), .out(subtractor_2_out));  // open: bin, bout

  // Notes on the sheet:
  //   if diff > 10 or not
endmodule
